// Logisim project Subtractor4bits.circ as structural Verilog
module Full_Adder (
  input  A,
  input  B,
  input  Cin,
  output Sum,
  output Cout
);

  wire and_1_out, and_2_out, xor_1_out;

  xor xor_1 (xor_1_out, A, B);
  xor xor_2 (Sum, xor_1_out, Cin);
  and and_1 (and_1_out, Cin, xor_1_out);
  and and_2 (and_2_out, B, A);
  or or_1 (Cout, and_1_out, and_2_out);
endmodule

module FULL_subtractor (
  input  B3,
  input  A3,
  input  B2,
  input  A2,
  input  B1,
  input  A1,
  input  B0,
  input  A0,
  input  CIN,
  input  Cout,
  input  S3,
  input  S2,
  input  S1,
  input  S0,
  input  OVERFLOW
);

  wire full_adder_2_cout, full_adder_3_cout, full_adder_4_cout, xor_2_out, xor_3_out, xor_4_out, xor_5_out;

  xor xor_1 (OVERFLOW, Cout, full_adder_2_cout);
  xor xor_2 (xor_2_out, B3, CIN);
  Full_Adder full_adder_1 (.A(A3), .B(xor_2_out), .Cin(full_adder_2_cout), .Sum(S3), .Cout(Cout));
  xor xor_3 (xor_3_out, B2, CIN);
  Full_Adder full_adder_2 (.A(A2), .B(xor_3_out), .Cin(full_adder_3_cout), .Sum(S2), .Cout(full_adder_2_cout));
  xor xor_4 (xor_4_out, B1, CIN);
  Full_Adder full_adder_3 (.A(A1), .B(xor_4_out), .Cin(full_adder_4_cout), .Sum(S1), .Cout(full_adder_3_cout));
  xor xor_5 (xor_5_out, B0, CIN);
  Full_Adder full_adder_4 (.A(A0), .B(xor_5_out), .Cin(CIN), .Sum(S0), .Cout(full_adder_4_cout));
endmodule
